// Digital circuit subleq.dig as structural Verilog
module subleq (
  input  clk,
  input  in_2,
  input  in_3,
  input  in_4,
  input  in_5,
  input  in_6,
  input  in_7,
  input  in_8,
  input  in_9,
  input  in_10,
  input  in_11,
  input  in_12,
  input  in_13,
  input  in_14,
  input  in_15,
  input  in_16,
  input  in_17,
  input  in_18,
  input  in_19,
  input  in_20,
  input  in_21,
  input  in_22,
  input  in_23,
  input  in_24,
  input  in_25
);

  wire _7404_1_pin1, _7404_1_pin3, _7404_1_pin5, _7404_1_pin9, _7404_2_pin1, _7404_2_pin3, _7404_2_pin5,
       _7404_2_pin9, _7404_3_pin8, _7404_3_pin10, _7404_3_pin12, _7404_4_pin2, _7404_4_pin9, _7404_4_pin12,
       _7408_1_pin3, _7408_1_pin4, _7408_1_pin5, _7408_1_pin6, _7408_1_pin8, _7408_1_pin9, _7408_1_pin10,
       _7408_1_pin11, _7408_1_pin13, _7408_2_pin4, _7408_2_pin5, _7408_2_pin6, _7408_2_pin8, _7408_2_pin12,
       _7408_2_pin13, _7421_1_pin1, _7421_1_pin2, _7421_1_pin4, _7421_1_pin5, _7421_1_pin9, _7421_1_pin10,
       _7421_1_pin12, _7421_1_pin13, _7425_1_pin6, _7425_1_pin8, _7432_1_pin4, _7432_1_pin5, _7432_1_pin11,
       _7432_1_pin12, _7432_2_pin8, _7432_2_pin9, _7474_1_pin8, _7476_1_pin6, _7476_1_pin11, _74157_1_pin2,
       _74157_1_pin4, _74157_1_pin5, _74157_1_pin7, _74157_1_pin9, _74157_1_pin11, _74157_1_pin12,
       _74157_1_pin14, _74157_2_pin2, _74157_2_pin4, _74157_2_pin5, _74157_2_pin7, _74157_2_pin9,
       _74157_2_pin11, _74157_2_pin12, _74157_2_pin14, _74157_3_pin2, _74157_3_pin4, _74157_3_pin5,
       _74157_3_pin7, _74157_3_pin9, _74157_3_pin11, _74157_3_pin12, _74157_3_pin14, _74161_1_pin7,
       _74173_1_pin9, _74173_1_pin15, _74173_3_pin3, _74173_3_pin4, _74173_3_pin5, _74173_3_pin6,
       _74173_3_pin9, _74173_4_pin1, _74173_5_pin3, _74173_5_pin4, _74173_5_pin5, _74173_5_pin6,
       _74173_6_pin3, _74173_6_pin4, _74173_6_pin5, _74173_6_pin6, _74245_1_pin2, _74245_1_pin3,
       _74245_1_pin4, _74245_1_pin5, _74245_1_pin6, _74245_1_pin7, _74245_1_pin8, _74245_1_pin9,
       _74245_1_pin19, _74283_1_pin1, _74283_1_pin2, _74283_1_pin3, _74283_1_pin4, _74283_1_pin5,
       _74283_1_pin6, _74283_1_pin7, _74283_1_pin10, _74283_1_pin11, _74283_1_pin12, _74283_1_pin13,
       _74283_1_pin14, _74283_1_pin15, _74283_2_pin1, _74283_2_pin2, _74283_2_pin3, _74283_2_pin4,
       _74283_2_pin5, _74283_2_pin6, _74283_2_pin10, _74283_2_pin11, _74283_2_pin12, _74283_2_pin13,
       _74283_2_pin14, _74283_2_pin15, and_1_out, counter_1_ovf, dipswitch_14_out, dipswitch_15_out,
       dipswitch_16_out, dipswitch_17_out, dipswitch_18_out, dipswitch_19_out, dipswitch_20_out,
       dipswitch_21_out, not_1_out;
  wire [7:0] counter_1_out;

  LED led_1 (.in(_74283_1_pin14));
  LED led_2 (.in(_74283_1_pin12));
  LED led_3 (.in(_74283_1_pin5));
  LED led_4 (.in(_74283_1_pin3));
  LED led_5 (.in(_74283_2_pin14));
  LED led_6 (.in(_74283_2_pin12));
  LED led_7 (.in(_74283_2_pin5));
  LED led_8 (.in(_74283_2_pin3));
  _74283 _74283_1 (
    .pin1(_74283_1_pin1), .pin2(_74283_1_pin2), .pin3(_74283_1_pin3), .pin4(_74283_1_pin4),
    .pin5(_74283_1_pin5), .pin6(_74283_1_pin6), .pin7(_74283_1_pin7), .pin8(1'b0), .pin10(_74283_1_pin10),
    .pin11(_74283_1_pin11), .pin12(_74283_1_pin12), .pin13(_74283_1_pin13), .pin14(_74283_1_pin14),
    .pin15(_74283_1_pin15), .pin16(1'b1));  // open: pin9
  _74283 _74283_2 (
    .pin1(_74283_2_pin1), .pin2(_74283_2_pin2), .pin3(_74283_2_pin3), .pin4(_74283_2_pin4),
    .pin5(_74283_2_pin5), .pin6(_74283_2_pin6), .pin7(1'b1), .pin8(1'b0), .pin9(_74283_1_pin7),
    .pin10(_74283_2_pin10), .pin11(_74283_2_pin11), .pin12(_74283_2_pin12), .pin13(_74283_2_pin13),
    .pin14(_74283_2_pin14), .pin15(_74283_2_pin15), .pin16(1'b1));
  _7404 _7404_1 (
    .pin1(_7404_1_pin1), .pin2(_74283_1_pin5), .pin3(_7404_1_pin3), .pin4(_74283_1_pin3),
    .pin5(_7404_1_pin5), .pin6(_74283_1_pin14), .pin7(1'b0), .pin8(_74283_1_pin12), .pin9(_7404_1_pin9),
    .pin11(1'b0), .pin13(1'b0), .pin14(1'b1));  // open: pin10, pin12
  _7404 _7404_2 (
    .pin1(_7404_2_pin1), .pin2(_74283_2_pin5), .pin3(_7404_2_pin3), .pin4(_74283_2_pin3),
    .pin5(_7404_2_pin5), .pin6(_74283_2_pin14), .pin7(1'b0), .pin8(_74283_2_pin12), .pin9(_7404_2_pin9),
    .pin11(1'b0), .pin13(1'b0), .pin14(1'b1));  // open: pin10, pin12
  _74173 _74173_1 (
    .pin1(1'b0), .pin2(1'b0), .pin3(_74283_1_pin6), .pin4(_74283_1_pin2), .pin5(_74283_1_pin15),
    .pin6(_74283_1_pin11), .pin7(clk), .pin8(1'b0), .pin9(_74173_1_pin9), .pin10(_74173_1_pin9),
    .pin11(_7404_1_pin9), .pin12(_7404_1_pin5), .pin13(_7404_1_pin3), .pin14(_7404_1_pin1),
    .pin15(_74173_1_pin15), .pin16(1'b1));
  _74173 _74173_2 (
    .pin1(1'b0), .pin2(1'b0), .pin3(_74283_2_pin6), .pin4(_74283_2_pin2), .pin5(_74283_2_pin15),
    .pin6(_74283_2_pin11), .pin7(clk), .pin8(1'b0), .pin9(_74173_1_pin9), .pin10(_74173_1_pin9),
    .pin11(_7404_2_pin9), .pin12(_7404_2_pin5), .pin13(_7404_2_pin3), .pin14(_7404_2_pin1),
    .pin15(_74173_1_pin15), .pin16(1'b1));
  _74173 _74173_3 (
    .pin1(_74173_1_pin9), .pin2(_74173_1_pin9), .pin3(_74173_3_pin3), .pin4(_74173_3_pin4),
    .pin5(_74173_3_pin5), .pin6(_74173_3_pin6), .pin7(clk), .pin8(1'b0), .pin9(_74173_3_pin9),
    .pin10(_74173_3_pin9), .pin11(in_6), .pin12(in_5), .pin13(in_4), .pin14(in_3), .pin15(_74173_1_pin15),
    .pin16(1'b1));
  _74173 _74173_4 (
    .pin1(_74173_4_pin1), .pin2(_74173_4_pin1), .pin3(_74173_3_pin3), .pin4(_74173_3_pin4),
    .pin5(_74173_3_pin5), .pin6(_74173_3_pin6), .pin7(clk), .pin8(1'b0), .pin9(_74173_3_pin9),
    .pin10(_74173_3_pin9), .pin11(in_2), .pin12(in_8), .pin13(in_7), .pin14(in_9), .pin15(_74173_1_pin15),
    .pin16(1'b1));
  _74173 _74173_5 (
    .pin1(1'b0), .pin2(1'b0), .pin3(_74173_5_pin3), .pin4(_74173_5_pin4), .pin5(_74173_5_pin5),
    .pin6(_74173_5_pin6), .pin7(clk), .pin8(1'b0), .pin9(_74173_1_pin9), .pin10(_74173_1_pin9), .pin11(in_6),
    .pin12(in_5), .pin13(in_4), .pin14(in_3), .pin15(_74173_1_pin15), .pin16(1'b1));
  _74173 _74173_6 (
    .pin1(1'b0), .pin2(1'b0), .pin3(_74173_6_pin3), .pin4(_74173_6_pin4), .pin5(_74173_6_pin5),
    .pin6(_74173_6_pin6), .pin7(clk), .pin8(1'b0), .pin9(_74173_1_pin9), .pin10(_74173_1_pin9), .pin11(in_2),
    .pin12(in_8), .pin13(in_7), .pin14(in_9), .pin15(_74173_1_pin15), .pin16(1'b1));
  _7425 _7425_1 (
    .pin1(_74283_2_pin4), .pin2(_74283_2_pin1), .pin4(_74283_2_pin13), .pin5(_74283_2_pin10),
    .pin6(_7425_1_pin6), .pin7(1'b0), .pin8(_7425_1_pin8), .pin9(_74283_1_pin4), .pin10(_74283_1_pin1),
    .pin12(_74283_1_pin13), .pin13(_74283_1_pin10), .pin14(1'b1));  // open: pin3, pin11
  _7408 _7408_1 (
    .pin1(_7425_1_pin6), .pin2(_7425_1_pin8), .pin3(_7408_1_pin3), .pin4(_7408_1_pin4), .pin5(_7408_1_pin5),
    .pin6(_7408_1_pin6), .pin7(1'b0), .pin8(_7408_1_pin8), .pin9(_7408_1_pin9), .pin10(_7408_1_pin10),
    .pin11(_7408_1_pin11), .pin12(_7408_1_pin9), .pin13(_7408_1_pin13), .pin14(1'b1));
  _7408 _7408_2 (
    .pin1(1'b0), .pin2(1'b0), .pin4(_7408_2_pin4), .pin5(_7408_2_pin5), .pin6(_7408_2_pin6), .pin7(1'b0),
    .pin8(_7408_2_pin8), .pin9(_7408_1_pin8), .pin10(clk), .pin11(_7408_2_pin4), .pin12(_7408_2_pin12),
    .pin13(_7408_2_pin13), .pin14(1'b1));  // open: pin3
  _7421 _7421_1 (
    .pin1(_7421_1_pin1), .pin2(_7421_1_pin2), .pin4(_7421_1_pin4), .pin5(_7421_1_pin5), .pin6(_7408_1_pin4),
    .pin7(1'b0), .pin8(_7408_1_pin5), .pin9(_7421_1_pin9), .pin10(_7421_1_pin10), .pin12(_7421_1_pin12),
    .pin13(_7421_1_pin13), .pin14(1'b1));  // open: pin3, pin11
  _7432 _7432_1 (
    .pin1(_7408_1_pin3), .pin2(_74283_1_pin10), .pin3(_7408_1_pin10), .pin4(_7432_1_pin4),
    .pin5(_7432_1_pin5), .pin6(_7408_2_pin5), .pin7(1'b0), .pin9(1'b0), .pin10(1'b0), .pin11(_7432_1_pin11),
    .pin12(_7432_1_pin12), .pin13(_7408_1_pin11), .pin14(1'b1));  // open: pin8
  _7432 _7432_2 (
    .pin1(1'b0), .pin2(1'b0), .pin4(1'b0), .pin5(1'b0), .pin7(1'b0), .pin8(_7432_2_pin8),
    .pin9(_7432_2_pin9), .pin10(_74173_1_pin15), .pin12(1'b0), .pin13(_7408_2_pin8), .pin14(1'b1));  // open: pin3, pin6, pin11
  _7404 _7404_3 (
    .pin1(_74173_4_pin1), .pin2(_7408_1_pin9), .pin3(_74173_1_pin9), .pin4(_7432_1_pin4),
    .pin5(_74173_3_pin9), .pin6(_7432_1_pin5), .pin7(1'b0), .pin8(_7404_3_pin8), .pin9(_7432_2_pin8),
    .pin10(_7404_3_pin10), .pin11(_7408_1_pin8), .pin12(_7404_3_pin12), .pin13(_7432_1_pin11), .pin14(1'b1));
  _7404 _7404_4 (
    .pin1(clk), .pin2(_7404_4_pin2), .pin3(1'b0), .pin5(1'b0), .pin7(1'b0), .pin8(_7432_2_pin9),
    .pin9(_7404_4_pin9), .pin10(_7408_2_pin12), .pin11(_7408_1_pin6), .pin12(_7404_4_pin12),
    .pin13(_74173_1_pin15), .pin14(1'b1));  // open: pin4, pin6
  _7474 _7474_1 (
    .pin1(1'b1), .pin2(1'b0), .pin3(1'b0), .pin4(1'b1), .pin7(1'b0), .pin8(_7474_1_pin8),
    .pin9(_7408_1_pin13), .pin10(1'b1), .pin11(clk), .pin12(1'b1), .pin13(_7474_1_pin8), .pin14(1'b1));  // open: pin5, pin6
  _74161 _74161_1 (
    .pin1(_7404_4_pin12), .pin2(clk), .pin3(_74173_5_pin3), .pin4(_74173_5_pin4), .pin5(_74173_5_pin5),
    .pin6(_74173_5_pin6), .pin7(_74161_1_pin7), .pin8(1'b0), .pin9(_7404_3_pin10), .pin10(_74161_1_pin7),
    .pin11(_7421_1_pin1), .pin12(_7421_1_pin2), .pin13(_7421_1_pin4), .pin14(_7421_1_pin5), .pin16(1'b1));  // open: pin15
  _74161 _74161_2 (
    .pin1(_7404_4_pin12), .pin2(clk), .pin3(_74173_6_pin3), .pin4(_74173_6_pin4), .pin5(_74173_6_pin5),
    .pin6(_74173_6_pin6), .pin7(_7408_2_pin6), .pin8(1'b0), .pin9(_7404_3_pin10), .pin10(_7408_2_pin6),
    .pin11(_7421_1_pin13), .pin12(_7421_1_pin12), .pin13(_7421_1_pin10), .pin14(_7421_1_pin9),
    .pin15(_74161_1_pin7), .pin16(1'b1));
  DipSwitch dipswitch_1 (.out(_7408_2_pin13));
  _74157 _74157_1 (
    .pin1(_7408_2_pin13), .pin2(_74157_1_pin2), .pin3(_74173_3_pin3), .pin4(_74157_1_pin4),
    .pin5(_74157_1_pin5), .pin6(_74173_3_pin4), .pin7(_74157_1_pin7), .pin8(1'b0), .pin9(_74157_1_pin9),
    .pin10(_74173_3_pin5), .pin11(_74157_1_pin11), .pin12(_74157_1_pin12), .pin13(_74173_3_pin6),
    .pin14(_74157_1_pin14), .pin15(1'b0), .pin16(1'b1));
  DipSwitch dipswitch_2 (.out(_74157_1_pin14));
  DipSwitch dipswitch_3 (.out(_74157_1_pin11));
  DipSwitch dipswitch_4 (.out(_74157_1_pin5));
  DipSwitch dipswitch_5 (.out(_74157_1_pin2));
  _74157 _74157_2 (
    .pin1(_7408_2_pin13), .pin2(_74157_2_pin2), .pin3(_74283_1_pin4), .pin4(_74157_2_pin4),
    .pin5(_74157_2_pin5), .pin6(_74283_1_pin1), .pin7(_74157_2_pin7), .pin8(1'b0), .pin9(_74157_2_pin9),
    .pin10(_74283_1_pin13), .pin11(_74157_2_pin11), .pin12(_74157_2_pin12), .pin13(_74283_1_pin10),
    .pin14(_74157_2_pin14), .pin15(1'b0), .pin16(1'b1));
  _74157 _74157_3 (
    .pin1(_7408_2_pin13), .pin2(_74157_3_pin2), .pin3(_74283_2_pin4), .pin4(_74157_3_pin4),
    .pin5(_74157_3_pin5), .pin6(_74283_2_pin1), .pin7(_74157_3_pin7), .pin8(1'b0), .pin9(_74157_3_pin9),
    .pin10(_74283_2_pin13), .pin11(_74157_3_pin11), .pin12(_74157_3_pin12), .pin13(_74283_2_pin10),
    .pin14(_74157_3_pin14), .pin15(1'b0), .pin16(1'b1));
  DipSwitch dipswitch_6 (.out(_74157_2_pin14));
  DipSwitch dipswitch_7 (.out(_74157_2_pin11));
  DipSwitch dipswitch_8 (.out(_74157_2_pin5));
  DipSwitch dipswitch_9 (.out(_74157_2_pin2));
  DipSwitch dipswitch_10 (.out(_74157_3_pin14));
  DipSwitch dipswitch_11 (.out(_74157_3_pin11));
  DipSwitch dipswitch_12 (.out(_74157_3_pin5));
  DipSwitch dipswitch_13 (.out(_74157_3_pin2));
  Button button_1 (.out(_7432_1_pin12));
  _74189 _74189_1 (
    .pin1(_74157_1_pin4), .pin2(1'b0), .pin3(_7404_3_pin12), .pin4(_74157_2_pin4), .pin5(_7404_1_pin1),
    .pin6(_74157_2_pin7), .pin7(_7404_1_pin3), .pin8(1'b0), .pin9(_7404_1_pin5), .pin10(_74157_2_pin9),
    .pin11(_7404_1_pin9), .pin12(_74157_2_pin12), .pin13(_74157_1_pin12), .pin14(_74157_1_pin9),
    .pin15(_74157_1_pin7), .pin16(1'b1));
  _74189 _74189_2 (
    .pin1(_74157_1_pin4), .pin2(1'b0), .pin3(_7404_3_pin12), .pin4(_74157_3_pin4), .pin5(_7404_2_pin1),
    .pin6(_74157_3_pin7), .pin7(_7404_2_pin3), .pin8(1'b0), .pin9(_7404_2_pin5), .pin10(_74157_3_pin9),
    .pin11(_7404_2_pin9), .pin12(_74157_3_pin12), .pin13(_74157_1_pin12), .pin14(_74157_1_pin9),
    .pin15(_74157_1_pin7), .pin16(1'b1));
  LED led_9 (.in(in_14));
  LED led_10 (.in(counter_1_ovf));
  LED led_11 (.in(in_12));
  LED led_12 (.in(in_13));
  LED led_13 (.in(in_10));
  LED led_14 (.in(in_11));
  and and_1 (and_1_out, not_1_out, clk);
  LED led_15 (.in(in_15));
  LED led_16 (.in(in_16));
  LED led_17 (.in(in_17));
  not not_1 (not_1_out, counter_1_ovf);
  Counter #(.Bits(8)) counter_1 (.en(1'b1), .C(and_1_out), .clr(1'b0), .out(counter_1_out), .ovf(counter_1_ovf));
  ROM #(.AddrBits(8), .Bits(8)) rom_1 (
    .A(counter_1_out), .sel(1'b1), .D({in_22, in_21, in_20, in_19, in_18, in_24, in_23, in_25}));
  // _28c16 _28c16_1: pin names not known; wires that end beside it: 1'b1, _7421_1_pin1, 1'b0, _7421_1_pin2, 1'b0, _7421_1_pin4, 1'b1, _7421_1_pin5, 1'b0, _7421_1_pin13, 1'b0, _7421_1_pin12, 1'b0, _7421_1_pin10, _7421_1_pin9, 1'b0
  _7476 _7476_1 (
    .pin1(_7404_4_pin2), .pin2(1'b1), .pin3(_7404_3_pin8), .pin4(_7408_2_pin4), .pin5(1'b1),
    .pin6(_7476_1_pin6), .pin7(1'b1), .pin8(_7404_3_pin8), .pin9(1'b1), .pin11(_7476_1_pin11), .pin12(1'b1),
    .pin13(1'b0), .pin15(_7476_1_pin6), .pin16(_7408_2_pin4));  // open: pin10, pin14
  _74245 _74245_1 (
    .pin1(1'b1), .pin2(_74245_1_pin2), .pin3(_74245_1_pin3), .pin4(_74245_1_pin4), .pin5(_74245_1_pin5),
    .pin6(_74245_1_pin6), .pin7(_74245_1_pin7), .pin8(_74245_1_pin8), .pin9(_74245_1_pin9), .pin10(1'b0),
    .pin11(in_14), .pin12(in_13), .pin13(in_12), .pin14(in_11), .pin15(in_10), .pin16(in_16), .pin17(in_15),
    .pin18(in_17), .pin19(_74245_1_pin19), .pin20(1'b1));
  _74139 _74139_1 (
    .pin1(1'b1), .pin2(1'b0), .pin3(1'b0), .pin8(1'b0), .pin9(_7404_4_pin9), .pin10(_74173_4_pin1),
    .pin11(_74173_1_pin9), .pin12(_74173_3_pin9), .pin13(_7476_1_pin11), .pin14(_7476_1_pin6), .pin15(1'b0),
    .pin16(1'b1));  // open: pin4, pin5, pin6, pin7
  DipSwitch dipswitch_14 (.out(dipswitch_14_out));
  DipSwitch dipswitch_15 (.out(dipswitch_15_out));
  DipSwitch dipswitch_16 (.out(dipswitch_16_out));
  DipSwitch dipswitch_17 (.out(dipswitch_17_out));
  DipSwitch dipswitch_18 (.out(dipswitch_18_out));
  DipSwitch dipswitch_19 (.out(dipswitch_19_out));
  DipSwitch dipswitch_20 (.out(dipswitch_20_out));
  DipSwitch dipswitch_21 (.out(dipswitch_21_out));
  DipSwitch dipswitch_22 (.out(_74245_1_pin9));
  DipSwitch dipswitch_23 (.out(_74245_1_pin8));
  DipSwitch dipswitch_24 (.out(_74245_1_pin7));
  DipSwitch dipswitch_25 (.out(_74245_1_pin6));
  LED led_18 (.in(clk));
  DipSwitch dipswitch_26 (.out(_74245_1_pin5));
  DipSwitch dipswitch_27 (.out(_74245_1_pin4));
  DipSwitch dipswitch_28 (.out(_74245_1_pin3));
  DipSwitch dipswitch_29 (.out(_74245_1_pin2));
  Button #(.activeLow("true")) button_2 (.out(_74245_1_pin19));
  Button button_3 (.out(_74173_1_pin15));

  // Notes on the sheet:
  //   clk: Hz: 500
  //   contents of rom_1 (hex, n*v repeats v):
  //   22,2,f,4,f2,6,ff,8,33,a,1f,c,f3,e,ff,10,0,12,f2,16,ff,2e,2f,18,fd,1a,22,1c,d2,1e,
  //   dd,20,ff,22,3f,24,fd,26,33,28,d3,2a,dd,2c,ff,2e,2f,32,ff,36,ff,34,f2,44,3f,38,f0,
  //   3a,ff,3c,ef,3e,f2,40,ff,42,ff,2e,ff,ff
endmodule
